# Fritzing sketch So_Do_Dau_Day_FinalCheck (saved by Fritzing 0.9.5d)
circuit board: 8.46667cm x 5.64444cm

parts:
  Part1 = Arduino Nano (Rev3.0) (ICSP)
  HC-SR04_Sensor_1 = HC-SR04 Ultrasonic Distance Sensor
  HC-SR04_Sensor_2 = HC-SR04 Ultrasonic Distance Sensor
  HC-SR04_Sensor_3 = HC-SR04 Ultrasonic Distance Sensor
  M2 = DC Motor
  L298N1 = L298N DC motor driver
  M3 = DC Motor
  S2 = Toggle Switch spst [package=THT]
  VCC1 = Battery [part_number=2]

nets:
  N1: Part1.D2, L298N1.IN1
  N2: Part1.D3, L298N1.IN2
  N3: Part1.D4, L298N1.IN3
  N4: Part1.D7, L298N1.IN4
  N5: Part1.D10, HC-SR04_Sensor_2.TRIG
  N6: Part1.D11/MOSI, HC-SR04_Sensor_2.ECHO
  VIN: Part1.VIN, L298N1.12V, S2.COM
  GND: Part1.GND, HC-SR04_Sensor_1.GND, HC-SR04_Sensor_2.GND, HC-SR04_Sensor_3.GND, L298N1.GND, VCC1.-
  N7: Part1.A5, HC-SR04_Sensor_1.ECHO
  N8: Part1.A4, HC-SR04_Sensor_1.TRIG
  N9: Part1.A1, HC-SR04_Sensor_3.ECHO
  N10: Part1.A0, HC-SR04_Sensor_3.TRIG
  VCC: HC-SR04_Sensor_1.VCC, HC-SR04_Sensor_2.VCC, HC-SR04_Sensor_3.VCC, L298N1.5V
  N11: M2.pin_1, L298N1.OUT1
  N12: M2.pin_2, L298N1.OUT2
  N13: L298N1.OUT3, M3.pin_1
  N14: L298N1.OUT4, M3.pin_2
  N15: S2.L1, VCC1.+

custom parts:
  L298N DC motor driver: 2x DC motor driver with 78M05 positive voltage regulator (7..35 V) L298N: max 46 V, 2 A Set 5 V Enable jumper to enable 5 V regultor (needed for the L298N) and +5 V output at screw terminal or supply external +5 V at screw terminal Set ENA and/or ENB to +5 V to enable motor permanently or supply ENA and/or ENB with PWM signal IN1 and IN2 set rotation directory for motor A (OUT1/OUT2) IN2 and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
  Toggle Switch spst: Toggle Switch single pole single throw
  Battery: Your standard 2x AA battery pack (3 Volts)

// code stored in the sketch: Untitled2.ino
#include <NewPing.h>

/* =====================================================================
   HUGGY BEAR — Firmware Sumo — BẢN CHỐT DUY NHẤT
   Arduino Nano + L298N-clone (INA/INB/INC/IND, giữ jumper ENA/ENB mặc định)

   CẬP NHẬT THEO SƠ ĐỒ THẬT (So_Do_Dau_Day.fzz):
   - CHỈ 3 CẢM BIẾN: Front/Right/Left — đã bỏ hoàn toàn nhánh "cảm biến
     sau lưng" (enemyBehind/TRIG_BACK/ECHO_BACK) vì không có trong sơ đồ
   - Sơ đồ gốc có sẵn 2 tụ gốm (C2, C5) + 1 tụ hoá (C4) nhưng KHÔNG dùng
     trên phần cứng thật -> vẫn giữ nguyên cơ chế "COAST" (thả trôi
     20ms trước khi đảo chiều) + bỏ qua đọc cảm biến lúc coast, để bù
     lại phần lọc nhiễu mà tụ đáng lẽ đảm nhiệm

   CÒN THIẾU/CẦN LÀM TRƯỚC KHI THI ĐẤU:
   - Cảm biến biên (bắt buộc theo luật) — chưa có cả phần cứng lẫn code
===================================================================== */

// ---------- HIỆU CHỈNH THEO ĐỘNG CƠ ----------
const unsigned long TIME_FORWARD = 100;
const unsigned long TIME_LEFT    = 180;
const unsigned long TIME_RIGHT   = 180;

// Thời gian thả trôi trước khi áp hướng mới, chỉ khi hướng THỰC SỰ đổi.
// Bù cho việc không có tụ lọc trên mạch thật.
const unsigned long COAST_MS = 20;

// ---------- CHÂN ĐỘNG CƠ — theo đúng nhãn trên board (INA-IND) ----------
const int INA = 6, INB = 5;   // -> OUTA/OUTB = Motor trái
const int INC = 4, IND = 3;   // -> OUTC/OUTD = Motor phải

// ---------- CẢM BIẾN SIÊU ÂM — CHỈ 3 CÁI, KHỚP SƠ ĐỒ THẬT ----------
const int TRIG_FRONT = A1, ECHO_FRONT = A0;
const int TRIG_RIGHT = A5, ECHO_RIGHT = A4;
const int TRIG_LEFT  = 11, ECHO_LEFT  = 10;
const int MAX_DISTANCE = 50;

NewPing sonarFront(TRIG_FRONT, ECHO_FRONT, MAX_DISTANCE);
NewPing sonarRight(TRIG_RIGHT, ECHO_RIGHT, MAX_DISTANCE);
NewPing sonarLeft (TRIG_LEFT,  ECHO_LEFT,  MAX_DISTANCE);

int  distFront = 0, distRight = 0, distLeft = 0;
int  cntFront = 0,  cntRight = 0,  cntLeft = 0;
bool enemyFront = false, enemyRight = false, enemyLeft = false;
bool isTimeUp = false;

const unsigned long PING_INTERVAL_MS = 30;
unsigned long lastPingTime = 0;
uint8_t sensorIndex = 0;   // 0=Front, 1=Right, 2=Left

enum ActionPhase { AP_DECIDE, AP_COAST, AP_WAIT_TURN, AP_WAIT_FORWARD };
enum Move { MOVE_FORWARD, MOVE_LEFT, MOVE_RIGHT };

ActionPhase actionPhase = AP_DECIDE;
unsigned long phaseEndTime = 0;
Move currentMove = MOVE_FORWARD;         // hướng đang thực sự chạy
Move pendingMove = MOVE_FORWARD;         // hướng sẽ áp dụng sau coast
unsigned long pendingDuration = 0;
ActionPhase pendingResultPhase = AP_DECIDE;

void setup() {
  pinMode(INA, OUTPUT); pinMode(INB, OUTPUT);
  pinMode(INC, OUTPUT); pinMode(IND, OUTPUT);
  stopMotors();
}

// ---------- ĐỘNG CƠ ----------
void forward() {
  digitalWrite(INA, HIGH); digitalWrite(INB, LOW);
  digitalWrite(INC, HIGH); digitalWrite(IND, LOW);
}
void left() {
  digitalWrite(INA, LOW);  digitalWrite(INB, HIGH);
  digitalWrite(INC, HIGH); digitalWrite(IND, LOW);
}
void right() {
  digitalWrite(INA, HIGH); digitalWrite(INB, LOW);
  digitalWrite(INC, LOW);  digitalWrite(IND, HIGH);
}
void stopMotors() {
  digitalWrite(INA, LOW); digitalWrite(INB, LOW);
  digitalWrite(INC, LOW); digitalWrite(IND, LOW);
}

void applyMove(Move m) {
  switch (m) {
    case MOVE_FORWARD: forward(); break;
    case MOVE_LEFT:    left();    break;
    case MOVE_RIGHT:   right();   break;
  }
}

// ---------- ĐỌC CẢM BIẾN — ROUND-ROBIN, NON-BLOCKING ----------
void updateFlag(int dist, int &counter, bool &flag) {
  if (dist > 0 && dist < MAX_DISTANCE) counter++; else counter = 0;
  flag = (counter >= 2);
}

void updateSensors() {
  // Bỏ qua đọc cảm biến đúng lúc đang coast — nhiễu điện dễ cao nhất
  // lúc này khi không có tụ lọc, dữ liệu đọc được kém tin cậy.
  if (actionPhase == AP_COAST) return;

  if (millis() - lastPingTime < PING_INTERVAL_MS) return;
  lastPingTime = millis();

  switch (sensorIndex) {
    case 0: distFront = sonarFront.ping_cm(); updateFlag(distFront, cntFront, enemyFront); break;
    case 1: distRight = sonarRight.ping_cm(); updateFlag(distRight, cntRight, enemyRight); break;
    case 2: distLeft  = sonarLeft.ping_cm();  updateFlag(distLeft,  cntLeft,  enemyLeft);  break;
  }
  sensorIndex = (sensorIndex + 1) % 3;
}

// ---------- MÁY TRẠNG THÁI TẤN CÔNG — NON-BLOCKING, CÓ COAST ----------
void queueMove(Move m, unsigned long duration, ActionPhase resultPhase) {
  if (m == currentMove) {
    // hướng không đổi -> không coast, tránh giật cục vô ích lúc đang quét
    actionPhase = resultPhase;
    phaseEndTime = millis() + duration;
    return;
  }
  stopMotors();
  pendingMove = m;
  pendingDuration = duration;
  pendingResultPhase = resultPhase;
  currentMove = m;
  actionPhase = AP_COAST;
  phaseEndTime = millis() + COAST_MS;
}

void runAttackStateMachine() {
  if (millis() < phaseEndTime) return;

  if (actionPhase == AP_COAST) {
    applyMove(pendingMove);
    actionPhase = pendingResultPhase;
    phaseEndTime = millis() + pendingDuration;
    return;
  }

  if (actionPhase == AP_WAIT_TURN) {   // vừa rẽ xong -> tiến tiếp
    queueMove(MOVE_FORWARD, TIME_FORWARD, AP_WAIT_FORWARD);
    return;
  }

  // AP_DECIDE hoặc vừa xong AP_WAIT_FORWARD -> đánh giá lại cảm biến
  if (enemyFront) {
    queueMove(MOVE_FORWARD, TIME_FORWARD, AP_WAIT_FORWARD);
  } else if (enemyRight) {
    queueMove(MOVE_RIGHT, TIME_RIGHT, AP_WAIT_TURN);
  } else if (enemyLeft) {
    queueMove(MOVE_LEFT, TIME_LEFT, AP_WAIT_TURN);
  } else {
    queueMove(MOVE_LEFT, 0, AP_DECIDE);   // quét mặc định — không tự chuyển sang forward
  }
}

void loop() {
  if (millis() > 5000) isTimeUp = true;

  updateSensors();
  if (!isTimeUp) return;

  runAttackStateMachine();
}
