# Fritzing sketch So_Do_Dau_Day (saved by Fritzing 0.9.5d)
circuit board: 8.46667cm x 5.64444cm

parts:
  Part1 = Arduino Nano (Rev3.0) (ICSP)
  HC-SR04_Sensor_1 = HC-SR04 Ultrasonic Distance Sensor
  HC-SR04_Sensor_2 = HC-SR04 Ultrasonic Distance Sensor
  HC-SR04_Sensor_3 = HC-SR04 Ultrasonic Distance Sensor
  C2 = Ceramic Capacitor [capacitance=100nF package="100 mil [THT, multilayer]"]
  C4 = Electrolytic Capacitor [capacitance=1µF package="100 mil [THT, electrolytic]"]
  M2 = DC Motor
  L298N1 = L298N DC motor driver
  C5 = Ceramic Capacitor [capacitance=100nF package="100 mil [THT, multilayer]"]
  M3 = DC Motor
  S2 = Toggle Switch spst [package=THT]
  VCC1 = Battery [part_number=2]

nets:
  N1: Part1.D2, L298N1.IN1
  N2: Part1.D3, L298N1.IN2
  N3: Part1.D4, L298N1.IN3
  N4: Part1.D7, L298N1.IN4
  N5: Part1.D10, HC-SR04_Sensor_2.TRIG
  N6: Part1.D11/MOSI, HC-SR04_Sensor_2.ECHO
  VIN: Part1.VIN, C4.-, L298N1.12V, S2.COM
  GND: Part1.GND, HC-SR04_Sensor_1.GND, HC-SR04_Sensor_2.GND, HC-SR04_Sensor_3.GND, L298N1.GND, VCC1.-
  N7: Part1.A5, HC-SR04_Sensor_1.ECHO
  N8: Part1.A4, HC-SR04_Sensor_1.TRIG
  N9: Part1.A1, HC-SR04_Sensor_3.ECHO
  N10: Part1.A0, HC-SR04_Sensor_3.TRIG
  VCC: HC-SR04_Sensor_1.VCC, HC-SR04_Sensor_2.VCC, HC-SR04_Sensor_3.VCC, L298N1.5V
  N11: C2.0, M2.pin_2, L298N1.OUT2
  N12: C2.1, M2.pin_1, L298N1.OUT1
  N13: L298N1.OUT3, C5.1, M3.pin_1
  N14: L298N1.OUT4, C5.0, M3.pin_2
  N15: S2.L1, VCC1.+

custom parts:
  L298N DC motor driver: 2x DC motor driver with 78M05 positive voltage regulator (7..35 V) L298N: max 46 V, 2 A Set 5 V Enable jumper to enable 5 V regultor (needed for the L298N) and +5 V output at screw terminal or supply external +5 V at screw terminal Set ENA and/or ENB to +5 V to enable motor permanently or supply ENA and/or ENB with PWM signal IN1 and IN2 set rotation directory for motor A (OUT1/OUT2) IN2 and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
  Toggle Switch spst: Toggle Switch single pole single throw
  Battery: Your standard 2x AA battery pack (3 Volts)

// code stored in the sketch: Untitled2.ino
#include <NewPing.h>


// --- C?U HÌNH TH?I GIAN ?I?U H??NG ---
#define TIME_FORWARD  100
#define TIME_LEFT     180
#define TIME_RIGHT    180
#define TIME_REVERSE  350


// --- C?U HÌNH CHÂN GIAO TI?P ---
// ??ng c? Trái (IN1, IN2)
const int IN1 = 6;
const int IN2 = 5;
// ??ng c? Ph?i (IN3, IN4)
const int IN3 = 4;
const int IN4 = 3;


// C?m bi?n Gi?a (Front)
const int TRIG_FRONT = A1;
const int ECHO_FRONT = A0;
// C?m bi?n Ph?i (Right)
const int TRIG_RIGHT = A5;
const int ECHO_RIGHT = A4;
// C?m bi?n Trái (Left)
const int TRIG_LEFT = 11;
const int ECHO_LEFT = 10;


const int MAX_DISTANCE = 50; // Quét t?i ?a 50cm trong ph?m vi sàn ??u


// Kh?i t?o ??i t??ng NewPing
NewPing sonarFront(TRIG_FRONT, ECHO_FRONT, MAX_DISTANCE);
NewPing sonarRight(TRIG_RIGHT, ECHO_RIGHT, MAX_DISTANCE);
NewPing sonarLeft(TRIG_LEFT, ECHO_LEFT, MAX_DISTANCE);


// --- BI?N TR?NG THÁI ---
int distFront = 0, distRight = 0, distLeft = 0;
int stateFront = 0, stateRight = 0, stateLeft = 0;
bool enemyFront = 0, enemyRight = 0, enemyLeft = 0;
bool enemyBehind = 1, isTimeUp = 0;


void setup() {
  // C?u hình chân ??ng c?
  pinMode(IN1, OUTPUT);
  pinMode(IN2, OUTPUT);
  pinMode(IN3, OUTPUT);
  pinMode(IN4, OUTPUT);
  
  // Led built-in (D13) báo hi?u khi b?t ???c m?c tiêu
  pinMode(13, OUTPUT);
  
  // Tr?ng thái an toàn: D?ng ??ng c? khi kh?i ??ng
  stopMotors();
}


// --- HÀM ?I?U KHI?N ??NG C? (C?u H L298N) ---
void forward() {
  digitalWrite(IN1, HIGH); digitalWrite(IN2, LOW);
  digitalWrite(IN3, HIGH); digitalWrite(IN4, LOW);
}


void left() {
  digitalWrite(IN1, LOW); digitalWrite(IN2, HIGH);
  digitalWrite(IN3, HIGH); digitalWrite(IN4, LOW);
}


void right() {
  digitalWrite(IN1, HIGH); digitalWrite(IN2, LOW);
  digitalWrite(IN3, LOW); digitalWrite(IN4, HIGH);
}


void stopMotors() {
  digitalWrite(IN1, LOW); digitalWrite(IN2, LOW);
  digitalWrite(IN3, LOW); digitalWrite(IN4, LOW);
}


void loop() {
  // 1. Logic tr? 5 giây ??u tr?n theo lu?t Sumo
  if (millis() > 5000) {
    isTimeUp = 1;
  }


  // 2. ??c kho?ng cách (Có delay 30ms ch?ng nhi?u chéo sóng âm)
  distFront = sonarFront.ping_cm(); delay(30);
  distRight = sonarRight.ping_cm(); delay(30);
  distLeft =  sonarLeft.ping_cm();  delay(30);


  // 3. B? l?c tr?ng thái (Debounce) cho C?m bi?n Gi?a
  if (distFront > 0 && distFront < MAX_DISTANCE) {
    stateFront++;
  } else {
    stateFront = 0;
  }
  
  if (stateFront >= 2) {
    enemyFront = 1;
    digitalWrite(13, HIGH);
  } else {
    enemyFront = 0;
    digitalWrite(13, LOW);
  }


  // 4. B? l?c tr?ng thái cho C?m bi?n Ph?i (Ch? quét n?u Gi?a không th?y ??i th?)
  if (enemyFront == 0) {
    if (distRight > 0 && distRight < MAX_DISTANCE) {
      stateRight++;
    } else {
      stateRight = 0;
    }
    
    if (stateRight >= 2) {
      enemyRight = 1;
      digitalWrite(13, HIGH);
    } else {
      enemyRight = 0;
      digitalWrite(13, LOW);
    }
  }


  // 5. B? l?c tr?ng thái cho C?m bi?n Trái (Ch? quét n?u Gi?a & Ph?i ??u không th?y)
  if (enemyFront == 0 && enemyRight == 0) {
    if (distLeft > 0 && distLeft < MAX_DISTANCE) {
      stateLeft++;
    } else {
      stateLeft = 0;
    }
    
    if (stateLeft >= 2) {
      enemyLeft = 1;
      digitalWrite(13, HIGH);
    } else {
      enemyLeft = 0;
      digitalWrite(13, LOW);
    }
  }


  // 6. MÁY TR?NG THÁI ?I?U H??NG T?N CÔNG (State Machine)
  if (isTimeUp == 1) {
    
    // ?u tiên 1: K? ??ch ? ngay phía tr??c -> Lao th?ng
    if (enemyFront == 1) {
      forward();
      enemyBehind = 0;
      delay(TIME_FORWARD);
    } 
    // ?u tiên 2: K? ??ch ? bên ph?i -> Xoay ph?i r?i lao t?i
    else if (enemyFront == 0 && enemyRight == 1) {
      right();
      delay(TIME_RIGHT);
      forward();
      enemyBehind = 0;
      delay(TIME_FORWARD);
    } 
    // ?u tiên 3: K? ??ch ? bên trái -> Xoay trái r?i lao t?i
    else if (enemyFront == 0 && enemyRight == 0 && enemyLeft == 1) {
      left();
      delay(TIME_LEFT);
      forward();
      enemyBehind = 0;
      delay(TIME_FORWARD);
    } 
    // K?ch b?n ??u tr?n: Không th?y ai -> Xoay 180 ?? tìm ki?m
    else if (enemyFront == 0 && enemyRight == 0 && enemyLeft == 0 && enemyBehind == 1) {
      left();
      delay(TIME_REVERSE);
      forward();
      enemyBehind = 0;
      delay(TIME_FORWARD);
    } 
    // Tr?ng thái quét m?c ??nh: Xoay tròn liên t?c ??n khi tìm th?y m?c tiêu
    else {
      left();
    }
  }
}
